# Fritzing sketch TemperatureController (saved by Fritzing 0.9.9b)
breadboards: 1

parts:
  Mod1 = Raspberry Pi 4B
  7SEG1 = 7-Segment LED I2C Backpack (blue)
  R1 = Resistor [tolerance=±5% power=0.25 resistance=3.3k package=THT]
  S1 = Pushbutton [package="[THT]"]
  R3 = Resistor [tolerance=±5% power=0.25 resistance=3.3k package=THT]
  S2 = Pushbutton [package="[THT]"]
  R7 = Resistor [tolerance=±5% power=0.25 resistance=10k package=THT]
  R8 = Resistor [tolerance=±5% power=0.25 resistance=4.7k package=THT]
  R9 = Resistor [tolerance=±5% power=0.25 resistance=4.7k package=THT]
  R10 = Resistor [tolerance=±5% power=0.25 resistance=4.7k package=THT]
  Piros = LED - 5mm [color="Red (633nm)" current=0.030 package="5 mm [THT]"]
  Fehér = LED - 5mm [color="White (4500K)" current=0.030 package="5 mm [THT]"]
  Zöld = LED - 5mm [color="Green (570nm)" current=0.030 package="5 mm [THT]"]
  Hőszabályzó_1 = DS18B20 1-Wire Temperature Sensor [part_number=DS18B20]
  Hőszabályzó_2 = DS18B20 1-Wire Temperature Sensor [part_number=DS18B20]
  Hőszabályzó_3 = DS18B20 1-Wire Temperature Sensor [part_number=DS18B20]
  Kék = LED - 5mm [color="Blue (525nm)" current=0.030 package="5 mm [THT]"]
  R6 = Resistor [tolerance=±5% power=0.25 resistance=4.7k package=THT]
  R11 = Resistor [tolerance=±5% power=0.25 resistance=10k package=THT]
  R12 = Resistor [tolerance=±5% power=0.25 resistance=4.7k package=THT]

nets:
  N1: Mod1.3V3, R7.Pin_0, R11.Pin_0
  VDD: Mod1.5V, 7SEG1.V+, Hőszabályzó_1.VDD, Hőszabályzó_2.VDD, Hőszabályzó_3.VDD, R12.Pin_0
  GND: Mod1.GND, 7SEG1.GND, S1.Pin_1, S1.Pin_2, S2.Pin_1, S2.Pin_2, Fehér.cathode, Zöld.cathode, Hőszabályzó_1.GND, Kék.cathode
  N2: Mod1.GPIO4, Hőszabályzó_1.DQ, Hőszabályzó_2.DQ, Hőszabályzó_3.DQ, R12.Pin_1
  N3: Mod1.GPIO14, R10.Pin_0
  N4: Mod1.GPIO15, R9.Pin_0
  N5: Mod1.GPIO18, R8.Pin_0
  N6: Mod1.GPIO23, R3.Pin_0
  N7: Mod1.GPIO24, R1.Pin_0
  N8: Mod1.ID_SD, 7SEG1.SCL
  N9: Mod1.GPIO5, 7SEG1.SDA
  N10: Mod1.GPIO12, R6.Pin_0
  N11: R1.Pin_1, S1.Pin_3, S1.Pin_4, R11.Pin_1
  N12: R3.Pin_1, S2.Pin_3, S2.Pin_4, R7.Pin_1
  N13: R8.Pin_1, Zöld.anode
  N14: R9.Pin_1, Fehér.anode
  N15: R10.Pin_1, Piros.anode
  GND_2: Piros.cathode, Hőszabályzó_2.GND, Hőszabályzó_3.GND
  N16: Kék.anode, R6.Pin_1

custom parts:
  7-Segment LED I2C Backpack (blue): 4-digit, 7-segment LED Display with I2C Control
